# Fritzing sketch CatFeeder (saved by Fritzing 0.9.3b)
breadboards: 1

parts:
  Motor_Shield = Adafruit DC+Stepper FeatherWing [part_number="Adafruit #2927"]
  Stepper_Motor = Stepper Motor - Bipolar
  Button = Round Pushbutton
  Controller = Adafruit Feather HUZZAH ESP8266 [part_number="Adafruit #2821"]
  Power_Supply = DC Power [voltage=12V]
  USB_Power_Supply = DC Power [voltage=5V]

nets:
  N1: Motor_Shield.SCL, Controller.GPIO5/SCL
  N2: Motor_Shield.SDA, Controller.GPIO4/SDA
  N3: Motor_Shield.GND, Power_Supply.V-
  N4: Motor_Shield.VMOTOR, Power_Supply.V+
  N5: Motor_Shield.M1B, Stepper_Motor.B
  N6: Motor_Shield.M1A, Stepper_Motor.D
  N7: Motor_Shield.M2A, Stepper_Motor.A
  N8: Motor_Shield.M2B, Stepper_Motor.C
  N9: Button.leg0, Controller.GPIO12/MISO
  N10: Button.leg1, Controller.GND, USB_Power_Supply.V-
  N11: Controller.VBUS, USB_Power_Supply.V+

custom parts:
  Adafruit DC+Stepper FeatherWing: This is the DC Motor + Stepper FeatherWing which will let you use 2 x bi-polar stepper motors or 4 x brushed DC motorx (or 1 stepper and 2 DC motors). Using our Feather Stacking Headers or Feather Female Headers you can connect a FeatherWing on top or bottom of your Feather board and let the board take flight! The original Adafruit Motorshield Kit is one of our most beloved kits, which is why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
  Adafruit Feather HUZZAH ESP8266: his is the Adafruit Feather HUZZAH ESP8266 - our take on an 'all-in-one' ESP8266 WiFi development board with built in USB and battery charging. Its an ESP8266 WiFi module with all the extras you need, ready to rock! We have other boards in the Feather family, check'em out here. At the Feather HUZZAH's heart is an ESP8266 WiFi microcontroller clocked at 80 MHz and at 3.3V logic. This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
